# Fritzing sketch Schematic (saved by Fritzing 0.9.10b)
breadboards: 1

parts:
  Part1 = Arduino Uno (Rev3)
  U1 = POT [knob_status=50% power=0.5W package=pot_mammoth]
  U2 = POT [knob_status=50% power=0.5W package=pot_mammoth]
  U3 = POT [knob_status=50% power=0.5W package=pot_mammoth]
  LED1 = RGB LED (com. cathode, rgb) [package="5 mm [THT]"]

nets:
  N1: Part1.A0, U3.A
  N2: Part1.A1, U2.A
  N3: Part1.A2, U1.A
  N4: Part1.D3_PWM, LED1.red_anode
  N5: Part1.D5_PWM, LED1.green_anode
  N6: Part1.D6_PWM, LED1.blue_anode
  N7: Part1.5V, U1.S, U2.S, U3.S
  N8: Part1.GND, U1.E, U2.E, U3.E, LED1.common_cathode
